// Logisim project SUMLAT.circ as structural Verilog: 1 circuit, main circuit main
module main (
  input  a1,
  input  b1,
  input  a0,
  input  b0,
  input  a5,
  input  b5,
  input  a4,
  input  b4,
  input  a3,
  input  b3,
  input  a2,
  input  b2,
  input  a7,
  input  b7,
  input  a6,
  input  b6,
  input  c0,
  output s0,
  output s1,
  output s2,
  output s3,
  output s4,
  output s5,
  output s6,
  output s7,
  output s8
);

  wire and_2_out, and_3_out, and_4_out, and_5_out, and_6_out, and_8_out, and_10_out, and_11_out, and_12_out,
       and_13_out, and_14_out, and_16_out, and_18_out, and_19_out, and_20_out, and_21_out, and_22_out,
       and_24_out, and_26_out, and_27_out, and_28_out, and_29_out, and_30_out, and_33_out, and_34_out,
       and_35_out, and_36_out, and_37_out, and_38_out, and_40_out, and_42_out, and_43_out, and_44_out,
       and_45_out, and_46_out, and_48_out, and_50_out, and_51_out, and_52_out, and_53_out, and_54_out,
       and_56_out, and_58_out, and_59_out, and_60_out, and_61_out, c1, c2, c3, c4, c5, c6, c7, g0, g1, G1_0,
       g2, g3, G3_0, G3_2, g4, g5, G5_4, g6, g7, G7_0, G7_4, G7_6, not_1_out, not_2_out, not_3_out,
       not_4_out, not_5_out, not_6_out, not_7_out, not_8_out, not_9_out, not_10_out, not_11_out, not_12_out,
       not_13_out, not_14_out, not_15_out, not_16_out, not_17_out, not_18_out, not_19_out, not_20_out,
       not_21_out, not_22_out, not_23_out, not_24_out, not_25_out, not_26_out, not_27_out, not_28_out,
       not_29_out, not_30_out, not_31_out, not_32_out, or_4_out, or_9_out, or_14_out, or_18_out, or_24_out,
       or_29_out, or_33_out, or_38_out, p0, p1, P1_0, p2, p3, P3_0, P3_2, p4, p5, P5_4, p6, P7_0, P7_4, P7_6;

  and and_1 (g7, b7, a7);
  or or_1 (s8, b7, a7);
  and and_2 (and_2_out, or_4_out, not_2_out);
  and and_3 (and_3_out, p6, c6);
  or or_2 (c7, and_3_out, g6);
  not not_1 (not_1_out, b7);
  and and_4 (and_4_out, a7, not_1_out);
  not not_2 (not_2_out, c7);
  and and_5 (and_5_out, c7, not_4_out);
  or or_3 (s7, and_2_out, and_5_out);
  not not_3 (not_3_out, a7);
  and and_6 (and_6_out, not_3_out, b7);
  or or_4 (or_4_out, and_4_out, and_6_out);
  not not_4 (not_4_out, or_4_out);
  and and_7 (P7_6, s8, p6);
  and and_8 (and_8_out, s8, g6);
  or or_5 (G7_6, and_8_out, g7);
  and and_9 (g6, b6, a6);
  or or_6 (p6, b6, a6);
  not not_5 (not_5_out, c6);
  and and_10 (and_10_out, or_9_out, not_5_out);
  or or_7 (s6, and_10_out, and_13_out);
  and and_11 (and_11_out, P5_4, c4);
  or or_8 (c6, and_11_out, G5_4);
  not not_6 (not_6_out, b6);
  not not_7 (not_7_out, a6);
  and and_12 (and_12_out, a6, not_6_out);
  or or_9 (or_9_out, and_12_out, and_14_out);
  not not_8 (not_8_out, or_9_out);
  and and_13 (and_13_out, c6, not_8_out);
  and and_14 (and_14_out, not_7_out, b6);
  and and_15 (P7_4, P7_6, P5_4);
  and and_16 (and_16_out, P7_6, G5_4);
  or or_10 (G7_4, and_16_out, G7_6);
  and and_17 (g5, b5, a5);
  or or_11 (p5, b5, a5);
  and and_18 (and_18_out, p4, c4);
  not not_9 (not_9_out, c5);
  and and_19 (and_19_out, or_14_out, not_9_out);
  or or_12 (s5, and_19_out, and_21_out);
  or or_13 (c5, and_18_out, g4);
  not not_10 (not_10_out, b5);
  not not_11 (not_11_out, a5);
  and and_20 (and_20_out, a5, not_10_out);
  or or_14 (or_14_out, and_20_out, and_22_out);
  not not_12 (not_12_out, or_14_out);
  and and_21 (and_21_out, c5, not_12_out);
  and and_22 (and_22_out, not_11_out, b5);
  and and_23 (P5_4, p5, p4);
  and and_24 (and_24_out, p5, g4);
  or or_15 (G5_4, and_24_out, g5);
  and and_25 (g4, b4, a4);
  or or_16 (p4, b4, a4);
  and and_26 (and_26_out, or_18_out, not_14_out);
  not not_13 (not_13_out, b4);
  and and_27 (and_27_out, a4, not_13_out);
  not not_14 (not_14_out, c4);
  and and_28 (and_28_out, c4, not_16_out);
  or or_17 (s4, and_26_out, and_28_out);
  not not_15 (not_15_out, a4);
  and and_29 (and_29_out, not_15_out, b4);
  or or_18 (or_18_out, and_27_out, and_29_out);
  not not_16 (not_16_out, or_18_out);
  and and_30 (and_30_out, P3_0, c0);
  or or_19 (c4, and_30_out, G3_0);
  and and_31 (P7_0, P7_4, P3_0);
  and and_32 (g3, b3, a3);
  or or_20 (p3, b3, a3);
  and and_33 (and_33_out, P7_4, G3_0);
  or or_21 (G7_0, and_33_out, G7_4);
  and and_34 (and_34_out, or_24_out, not_18_out);
  and and_35 (and_35_out, p2, c2);
  or or_22 (c3, and_35_out, g2);
  not not_17 (not_17_out, b3);
  and and_36 (and_36_out, a3, not_17_out);
  not not_18 (not_18_out, c3);
  and and_37 (and_37_out, c3, not_20_out);
  or or_23 (s3, and_34_out, and_37_out);
  not not_19 (not_19_out, a3);
  and and_38 (and_38_out, not_19_out, b3);
  or or_24 (or_24_out, and_36_out, and_38_out);
  not not_20 (not_20_out, or_24_out);
  and and_39 (P3_2, p3, p2);
  and and_40 (and_40_out, p3, g2);
  or or_25 (G3_2, and_40_out, g3);
  and and_41 (g2, b2, a2);
  or or_26 (p2, b2, a2);
  not not_21 (not_21_out, c2);
  and and_42 (and_42_out, or_29_out, not_21_out);
  or or_27 (s2, and_42_out, and_45_out);
  and and_43 (and_43_out, P1_0, c0);
  or or_28 (c2, and_43_out, G1_0);
  not not_22 (not_22_out, b2);
  not not_23 (not_23_out, a2);
  and and_44 (and_44_out, a2, not_22_out);
  or or_29 (or_29_out, and_44_out, and_46_out);
  not not_24 (not_24_out, or_29_out);
  and and_45 (and_45_out, c2, not_24_out);
  and and_46 (and_46_out, not_23_out, b2);
  and and_47 (P3_0, P3_2, P1_0);
  and and_48 (and_48_out, P3_2, G1_0);
  or or_30 (G3_0, and_48_out, G3_2);
  and and_49 (g1, b1, a1);
  or or_31 (p1, b1, a1);
  and and_50 (and_50_out, p0, c0);
  not not_25 (not_25_out, c1);
  and and_51 (and_51_out, or_33_out, not_25_out);
  or or_32 (c1, and_50_out, g0);
  not not_26 (not_26_out, b1);
  and and_52 (and_52_out, a1, not_26_out);
  or or_33 (or_33_out, and_52_out, and_54_out);
  not not_27 (not_27_out, or_33_out);
  and and_53 (and_53_out, c1, not_27_out);
  or or_34 (s1, and_51_out, and_53_out);
  not not_28 (not_28_out, a1);
  and and_54 (and_54_out, not_28_out, b1);
  and and_55 (P1_0, p1, p0);
  and and_56 (and_56_out, p1, g0);
  or or_35 (G1_0, and_56_out, g1);
  and and_57 (g0, b0, a0);
  or or_36 (p0, b0, a0);
  and and_58 (and_58_out, a0, not_30_out);
  not not_29 (not_29_out, c0);
  and and_59 (and_59_out, or_38_out, not_29_out);
  or or_37 (s0, and_59_out, and_61_out);
  not not_30 (not_30_out, b0);
  not not_31 (not_31_out, a0);
  and and_60 (and_60_out, not_31_out, b0);
  or or_38 (or_38_out, and_58_out, and_60_out);
  not not_32 (not_32_out, or_38_out);
  and and_61 (and_61_out, c0, not_32_out);

  // Other names for the same wires on the sheet: p7 = s8
endmodule
